# Fritzing sketch Potentiometer (saved by Fritzing 1.0.0rc)
breadboards: 1

parts:
  Part1 = Arduino Uno (Rev3)
  R1 = Resistor [tolerance=±5% power=0.25W resistance=220 package=THT]
  LED2 = LED - 5mm [color="Red (633nm)" current=0.030A package="5 mm [THT]"]
  POT1 = Breadboard Trimpot

nets:
  N1: Part1.A0, POT1.PIN2
  N2: Part1.D13/SCK, LED2.anode
  N3: Part1.5V, POT1.PIN1
  N4: Part1.GND, R1.Pin_0, POT1.PIN3
  N5: R1.Pin_1, LED2.cathode

notes:
  330Ω Resistor
  Short Leg LED (–) Cathode
