# Fritzing sketch Multiple LEDs (saved by Fritzing 1.0.0rc)
breadboards: 1

parts:
  Part1 = Arduino Uno (Rev3)
  R1 = Resistor [tolerance=±5% power=0.25W resistance=220 package=THT]
  LED2 = LED - 5mm [color="Red (633nm)" current=0.030A package="5 mm [THT]"]
  LED3 = LED - 5mm [color="Red (633nm)" current=0.030A package="5 mm [THT]"]
  LED4 = LED - 5mm [color="Red (633nm)" current=0.030A package="5 mm [THT]"]
  LED5 = LED - 5mm [color="Red (633nm)" current=0.030A package="5 mm [THT]"]
  LED6 = LED - 5mm [color="Red (633nm)" current=0.030A package="5 mm [THT]"]
  R2 = Resistor [tolerance=±5% power=0.25W resistance=220 package=THT]
  R3 = Resistor [tolerance=±5% power=0.25W resistance=220 package=THT]
  R4 = Resistor [tolerance=±5% power=0.25W resistance=220 package=THT]
  R5 = Resistor [tolerance=±5% power=0.25W resistance=220 package=THT]
  LED7 = LED - 5mm [color="Red (633nm)" current=0.030A package="5 mm [THT]"]
  LED8 = LED - 5mm [color="Red (633nm)" current=0.030A package="5 mm [THT]"]
  LED9 = LED - 5mm [color="Red (633nm)" current=0.030A package="5 mm [THT]"]
  R6 = Resistor [tolerance=±5% power=0.25W resistance=220 package=THT]
  R7 = Resistor [tolerance=±5% power=0.25W resistance=220 package=THT]
  R8 = Resistor [tolerance=±5% power=0.25W resistance=220 package=THT]

nets:
  N1: Part1.D8, LED4.anode
  N2: Part1.D9_PWM, LED2.anode
  N3: Part1.D2, LED9.anode
  N4: Part1.D3_PWM, LED8.anode
  N5: Part1.D4, LED7.anode
  N6: Part1.D5_PWM, LED6.anode
  N7: Part1.D6_PWM, LED5.anode
  N8: Part1.D7, LED3.anode
  N9: Part1.GND, R1.Pin_0, R2.Pin_0, R3.Pin_0, R4.Pin_0, R5.Pin_0, R6.Pin_0, R7.Pin_0, R8.Pin_0
  N10: R1.Pin_1, LED2.cathode
  N11: LED3.cathode, R3.Pin_1
  N12: LED4.cathode, R2.Pin_1
  N13: LED5.cathode, R4.Pin_1
  N14: LED6.cathode, R5.Pin_1
  N15: LED7.cathode, R6.Pin_1
  N16: LED8.cathode, R7.Pin_1
  N17: LED9.cathode, R8.Pin_1

notes:
  330Ω Resistors
  Short Leg LED (–) Cathode
