# Fritzing sketch pushbutton (saved by Fritzing 1.0.0rc)
breadboards: 1

parts:
  Part1 = Arduino Uno (Rev3)
  LED1 = smd LED [color="Red (633nm)" package="0603 [SMD]"]
  R1 = Resistor [tolerance=±5% resistance=220 package="0402 [SMD]"]
  R3 = Resistor [tolerance=±5% power=0.25W resistance=220 package=THT]
  R4 = Resistor [tolerance=±5% power=0.25W resistance=220 package=THT]
  S5 = Round Pushbutton
  S6 = Round Pushbutton

nets:
  N1: Part1.D13/SCK, LED1.anode
  N2: Part1.GND, R1.Pin_1, S5.leg1, S6.leg1
  N3: Part1.D2, R4.Pin_1, S6.leg0
  N4: Part1.D3_PWM, R3.Pin_1, S5.leg0
  N5: Part1.5V, R3.Pin_0, R4.Pin_0
  N6: LED1.cathode, R1.Pin_0

notes:
  330Ω Resistor
  Short Leg LED (–)
  10kΩ Resistors for buttons.
  Not pressed = HIGH 5V
  Pressed = LOW GND
