# Fritzing sketch led_fan (saved by Fritzing 1.0.0rc)
breadboards: 1

parts:
  Part1 = Arduino Uno (Rev3)
  LED1 = smd LED [color="Red (633nm)" package="0603 [SMD]"]
  R1 = Resistor [tolerance=±5% resistance=220 package="0402 [SMD]"]
  M1 = DC Motor [voltage_(max)=6V voltage_(min)=3V]

nets:
  N1: Part1.D12/MISO, M1.pin_2
  N2: Part1.D13/SCK, LED1.anode
  N3: Part1.GND, R1.Pin_1, M1.pin_1
  N4: LED1.cathode, R1.Pin_0

notes:
  330Ω Resistor
  Short Leg LED (–)
  Reversing motor leads will reverse its direction
