# Fritzing sketch button_gui (saved by Fritzing 1.0.0rc)
breadboards: 1

parts:
  Part1 = Arduino Uno (Rev3)
  LED1 = smd LED [color="Red (633nm)" package="0603 [SMD]"]
  R1 = Resistor [tolerance=±5% resistance=220 package="0402 [SMD]"]
  S1 = Pushbutton [package="[THT]"]
  R2 = Resistor [tolerance=±5% power=0.25W resistance=220 package=THT]

nets:
  N1: Part1.D13/SCK, LED1.anode
  N2: Part1.GND, R1.Pin_1, R2.Pin_0
  N3: Part1.D7, Part1.5V, S1.Pin_3, S1.Pin_4
  N4: LED1.cathode, R1.Pin_0

notes:
  330Ω Resistor
  Short Leg LED (–)
  10kΩ Resistor
  Short Leg LED (–)
