# Fritzing sketch photocell (saved by Fritzing 1.0.0rc)
breadboards: 1

parts:
  Part1 = Arduino Uno (Rev3)
  LED1 = smd LED [color="Red (633nm)" package="0603 [SMD]"]
  R1 = Resistor [tolerance=±5% resistance=220 package="0402 [SMD]"]
  R5 = PHOTOCELL [package=photocell]
  R6 = Resistor [tolerance=±5% power=0.25W resistance=220 package=THT]

nets:
  N1: Part1.A0, R1.Pin_0, R5.P$1
  N2: Part1.D9_PWM, LED1.anode
  N3: Part1.5V, R1.Pin_1
  N4: Part1.GND, R5.P$2, R6.Pin_0
  N5: LED1.cathode, R6.Pin_1

notes:
  330Ω Resistor
  Short Leg LED (–)
  10kΩ Resistor for photocell
